// Logisim project Versuch3_Augabe3.circ as structural Verilog: 1 circuit, main circuit main
module main (
);

  wire and_1_out, and_2_out, and_3_out, and_4_out, and_5_out, and_6_out, and_7_out, and_8_out, button_1_out,
       clock_1_out, d_ff_1_q, d_ff_2_q, d_ff_3_q, nand_1_out, nand_2_out, nand_3_out, nand_4_out, nand_5_out,
       nand_6_out, nand_7_out, nand_8_out, nand_9_out, nand_10_out, not_1_out, not_2_out, not_3_out,
       not_4_out, not_5_out, not_6_out, or_1_out, or_2_out, or_3_out;

  Clock clock_1 (.out(clock_1_out));
  not not_1 (not_1_out, clock_1_out);
  Button button_1 (.out(button_1_out));
  nand nand_1 (nand_1_out, clock_1_out, nand_2_out);
  nand nand_2 (nand_2_out, nand_1_out, not_1_out);
  not not_2 (not_2_out, nand_2_out);
  not not_3 (not_3_out, d_ff_1_q);
  not not_4 (not_4_out, nand_9_out);
  not not_5 (not_5_out, d_ff_2_q);
  not not_6 (not_6_out, d_ff_3_q);
  nand nand_3 (nand_3_out, not_4_out, not_2_out);
  nand nand_4 (nand_4_out, not_2_out, nand_9_out);
  nand nand_5 (nand_5_out, nand_3_out, nand_6_out);
  nand nand_6 (nand_6_out, nand_5_out, nand_4_out);
  and and_1 (and_1_out, d_ff_1_q, not_4_out);
  and and_2 (and_2_out, nand_9_out, not_3_out, not_6_out);
  and and_3 (and_3_out, d_ff_2_q, not_3_out);
  and and_4 (and_4_out, not_4_out, d_ff_2_q);
  and and_5 (and_5_out, nand_9_out, d_ff_1_q, not_5_out);
  and and_6 (and_6_out, d_ff_3_q, not_4_out);
  and and_7 (and_7_out, nand_9_out, d_ff_1_q, d_ff_2_q);
  nand nand_7 (nand_7_out, nand_5_out, nand_2_out);
  nand nand_8 (nand_8_out, nand_2_out, nand_6_out);
  and and_8 (and_8_out, nand_8_out, button_1_out);
  or or_1 (or_1_out, and_1_out, and_2_out);
  or or_2 (or_2_out, and_3_out, and_4_out, and_5_out);
  or or_3 (or_3_out, and_6_out, and_7_out);
  nand nand_9 (nand_9_out, nand_7_out, nand_10_out);
  nand nand_10 (nand_10_out, nand_9_out, and_8_out, and_8_out);
  D_Flip_Flop d_ff_1 (.clk(nand_2_out), .D(or_1_out), .Q(d_ff_1_q));  // open: Qn, preset, en, reset
  D_Flip_Flop d_ff_2 (.clk(nand_2_out), .D(or_2_out), .Q(d_ff_2_q));  // open: Qn, preset, en, reset
  D_Flip_Flop d_ff_3 (.clk(nand_2_out), .D(or_3_out), .Q(d_ff_3_q));  // open: Qn, preset, en, reset
endmodule
